# Fritzing sketch beer-monitor-schematics (saved by Fritzing 0.9.3b)
breadboards: 1

parts:
  U1 = NodeMCU V3.0
  DS1 = DS18B20 1-Wire Temperature Sensor [part_number=DS18B20]
  DS2 = DS18B20 1-Wire Temperature Sensor [part_number=DS18B20]
  R1 = Resistor [tolerance=±5% resistance=220 package="0402 [SMD]"]
  PIR1 = PIR sensor

nets:
  N1: U1.D2, PIR1.SIG
  N2: U1.D3, DS1.DQ, DS2.DQ, R1.Pin_1
  3V3: U1.3V3, PIR1.VDD
  GND: U1.GND, DS1.GND, DS2.GND, PIR1.GND
  VDD: U1.Vin, DS1.VDD, DS2.VDD, R1.Pin_0

custom parts:
  NodeMCU V3.0: ESP8266 based NodeMCU
